// Logisim project TP1.circ as structural Verilog: 5 circuits, main circuit main
module main (
  input  cin,
  input  a3,
  input  a2,
  input  a1,
  input  a0,
  input  b3,
  input  b2,
  input  b1,
  input  b0,
  output s3,
  output s2,
  output s1,
  output s0,
  output overflow,
  output cout
);

  wire decodificador_1_a, decodificador_1_b, decodificador_1_c, decodificador_1_d, decodificador_1_e,
       decodificador_1_f, decodificador_1_g, decodificador_2_a, decodificador_2_b, decodificador_2_c,
       decodificador_2_d, decodificador_2_e, decodificador_2_f, decodificador_2_g, decodificador_3_a,
       decodificador_3_b, decodificador_3_c, decodificador_3_d, decodificador_3_e, decodificador_3_f,
       decodificador_3_g;

  decodificador decodificador_1 (
    .h(a3), .x2(a2), .x3(a1), .x4(a0), .a(decodificador_1_a), .b(decodificador_1_b), .c(decodificador_1_c),
    .d(decodificador_1_d), .e(decodificador_1_e), .f(decodificador_1_f), .g(decodificador_1_g));
  decodificador decodificador_2 (
    .h(b3), .x2(b2), .x3(b1), .x4(b0), .a(decodificador_2_a), .b(decodificador_2_b), .c(decodificador_2_c),
    .d(decodificador_2_d), .e(decodificador_2_e), .f(decodificador_2_f), .g(decodificador_2_g));
  _7_Segment_Display u_7_segment_display_1 (
    .g(decodificador_1_a), .f(decodificador_1_b), .a(decodificador_1_c), .b(decodificador_1_d),
    .e(decodificador_1_e), .d(decodificador_1_f), .c(decodificador_1_g));  // open: dp
  somador_4bit somador_4bit_1 (
    .a0(a0), .a1(a1), .a2(a2), .a3(a3), .b0(b0), .b1(b1), .b2(b2), .b3(b3), .cin(cin), .s0(s0), .s1(s1),
    .s2(s2), .s3(s3), .cout(cout), .overflow(overflow));
  _7_Segment_Display u_7_segment_display_2 (
    .g(decodificador_2_a), .f(decodificador_2_b), .a(decodificador_2_c), .b(decodificador_2_d),
    .e(decodificador_2_e), .d(decodificador_2_f), .c(decodificador_2_g));  // open: dp
  decodificador decodificador_3 (
    .h(s3), .x2(s2), .x3(s1), .x4(s0), .a(decodificador_3_a), .b(decodificador_3_b), .c(decodificador_3_c),
    .d(decodificador_3_d), .e(decodificador_3_e), .f(decodificador_3_f), .g(decodificador_3_g));
  _7_Segment_Display u_7_segment_display_3 (
    .g(decodificador_3_a), .f(decodificador_3_b), .a(decodificador_3_c), .b(decodificador_3_d),
    .e(decodificador_3_e), .d(decodificador_3_f), .c(decodificador_3_g));  // open: dp
endmodule

module meio_somador (
  input  A0,
  input  B0,
  output S,
  output Cout
);

  xor xor_1 (S, A0, B0);
  and and_1 (Cout, A0, B0);
endmodule

module somador_completo (
  input  a,
  input  b,
  input  cin,
  output sum,
  output cout
);

  wire and_1_out, and_2_out, and_3_out, xor_1_out;

  and and_1 (and_1_out, b, cin);
  and and_2 (and_2_out, a, cin);
  and and_3 (and_3_out, a, b);
  xor xor_1 (xor_1_out, a, b);
  xor xor_2 (sum, xor_1_out, cin);
  or or_1 (cout, and_1_out, and_2_out, and_3_out);
endmodule

module decodificador (
  input  h,
  input  x2,
  input  x3,
  input  x4,
  output a,
  output b,
  output c,
  output d,
  output e,
  output f,
  output g
);

  wire and_1_out, and_2_out, and_3_out, and_4_out, and_5_out, and_6_out, and_7_out, and_8_out, and_9_out,
       and_10_out, and_11_out, and_12_out, and_13_out, and_14_out, and_15_out, and_16_out, and_17_out,
       and_18_out, and_19_out, and_20_out, and_21_out, and_22_out, and_23_out, and_24_out, and_25_out,
       and_26_out, and_27_out, and_28_out, and_29_out, and_30_out, and_31_out, and_32_out, not_1_out,
       not_2_out, not_3_out, not_4_out, not_5_out, not_6_out, not_7_out, not_8_out, not_9_out, not_10_out,
       not_11_out, not_12_out, not_13_out, not_14_out, not_15_out, not_16_out, not_17_out, not_18_out,
       not_19_out, not_20_out, not_21_out, not_22_out, not_23_out, not_24_out, not_25_out, not_26_out,
       not_27_out, not_28_out, not_29_out, not_30_out, not_31_out, not_32_out, not_33_out, not_34_out,
       not_35_out, not_36_out, not_37_out, not_38_out, not_39_out, not_40_out, not_41_out, not_42_out;

  not not_1 (not_1_out, x2);
  and and_1 (and_1_out, not_1_out, x3);
  and and_2 (and_2_out, x2, not_2_out);
  not not_2 (not_2_out, x3);
  and and_3 (and_3_out, x2, not_3_out);
  not not_3 (not_3_out, x4);
  not not_4 (not_4_out, h);
  not not_5 (not_5_out, x3);
  and and_4 (and_4_out, not_4_out, not_5_out, not_6_out);
  not not_6 (not_6_out, x4);
  not not_7 (not_7_out, h);
  and and_5 (and_5_out, not_7_out, x2, not_8_out);
  not not_8 (not_8_out, x3);
  not not_9 (not_9_out, h);
  and and_6 (and_6_out, not_9_out, x2, not_10_out);
  not not_10 (not_10_out, x4);
  and and_7 (and_7_out, h, not_11_out);
  not not_11 (not_11_out, x2);
  and and_8 (and_8_out, h, x3);
  not not_12 (not_12_out, x2);
  and and_9 (and_9_out, not_12_out, not_13_out);
  not not_13 (not_13_out, x4);
  not not_14 (not_14_out, h);
  and and_10 (and_10_out, not_14_out, x3);
  not not_15 (not_15_out, h);
  and and_11 (and_11_out, not_15_out, x2, x4);
  and and_12 (and_12_out, x2, x3);
  and and_13 (and_13_out, h, not_16_out, not_17_out);
  not not_16 (not_16_out, x2);
  not not_17 (not_17_out, x3);
  not not_18 (not_18_out, h);
  and and_14 (and_14_out, not_18_out, not_19_out);
  not not_19 (not_19_out, x2);
  not not_20 (not_20_out, h);
  not not_21 (not_21_out, x3);
  and and_15 (and_15_out, not_20_out, not_21_out, not_22_out);
  not not_22 (not_22_out, x4);
  not not_23 (not_23_out, x2);
  and and_16 (and_16_out, not_23_out, not_24_out);
  not not_24 (not_24_out, x4);
  not not_25 (not_25_out, h);
  and and_17 (and_17_out, not_25_out, x3, x4);
  not not_26 (not_26_out, x3);
  and and_18 (and_18_out, h, not_26_out, x4);
  not not_27 (not_27_out, x2);
  and and_19 (and_19_out, not_27_out, not_28_out);
  not not_28 (not_28_out, x4);
  and and_20 (and_20_out, x3, not_29_out);
  not not_29 (not_29_out, x4);
  and and_21 (and_21_out, h, x3);
  and and_22 (and_22_out, h, x2);
  not not_30 (not_30_out, h);
  not not_31 (not_31_out, x2);
  and and_23 (and_23_out, not_30_out, not_31_out, not_32_out);
  not not_32 (not_32_out, x4);
  not not_33 (not_33_out, x2);
  and and_24 (and_24_out, not_33_out, x3, x4);
  not not_34 (not_34_out, x3);
  and and_25 (and_25_out, x2, not_34_out, x4);
  and and_26 (and_26_out, x2, x3, not_35_out);
  not not_35 (not_35_out, x4);
  and and_27 (and_27_out, h, not_36_out);
  not not_36 (not_36_out, x3);
  not not_37 (not_37_out, h);
  and and_28 (and_28_out, not_37_out, not_38_out);
  not not_38 (not_38_out, x3);
  not not_39 (not_39_out, h);
  and and_29 (and_29_out, not_39_out, x4);
  not not_40 (not_40_out, x3);
  and and_30 (and_30_out, not_40_out, x4);
  not not_41 (not_41_out, h);
  and and_31 (and_31_out, not_41_out, x2);
  and and_32 (and_32_out, h, not_42_out);
  not not_42 (not_42_out, x2);
  or or_1 (a, and_1_out, and_2_out, and_3_out, h);
  or or_2 (b, and_4_out, and_5_out, and_6_out, and_7_out, and_8_out);
  or or_3 (c, and_9_out, and_10_out, and_11_out, and_12_out, and_13_out);
  or or_4 (d, and_14_out, and_15_out, and_16_out, and_17_out, and_18_out);
  or or_5 (e, and_19_out, and_20_out, and_21_out, and_22_out);
  or or_6 (f, and_23_out, and_24_out, and_25_out, and_26_out, and_27_out);
  or or_7 (g, and_28_out, and_29_out, and_30_out, and_31_out, and_32_out);
endmodule

module somador_4bit (
  input  cin,
  input  a0,
  input  a1,
  input  a2,
  input  a3,
  input  b0,
  input  b1,
  input  b2,
  input  b3,
  output s0,
  output s1,
  output s2,
  output s3,
  output cout,
  output overflow
);

  wire somador_completo_1_cout, somador_completo_2_cout, somador_completo_3_cout;

  somador_completo somador_completo_1 (.a(a0), .b(b0), .cin(cin), .sum(s0), .cout(somador_completo_1_cout));
  somador_completo somador_completo_2 (
    .a(a1), .b(b1), .cin(somador_completo_1_cout), .sum(s1), .cout(somador_completo_2_cout));
  somador_completo somador_completo_3 (
    .a(a2), .b(b2), .cin(somador_completo_2_cout), .sum(s2), .cout(somador_completo_3_cout));
  somador_completo somador_completo_4 (.a(a3), .b(b3), .cin(somador_completo_3_cout), .sum(s3), .cout(cout));

  assign overflow = cout;
endmodule
